// Digital circuit alu_math.dig as structural Verilog
module alu_math (
  input  A_0,
  input  A_1,
  input  A_2,
  input  A_3,
  input  A_4,
  input  A_5,
  input  A_6,
  input  A_7,
  input  B_0,
  input  B_1,
  input  B_2,
  input  B_3,
  input  B_4,
  input  B_5,
  input  B_6,
  input  B_7,
  input  SUB
);

  wire _74283_1_pin1, _74283_1_pin4, _74283_1_pin9, _74283_1_pin10, _74283_1_pin11, _74283_1_pin13,
       _74283_1_pin15, _74283_2_pin1, _74283_2_pin4, _74283_2_pin9, _74283_2_pin10, _74283_2_pin11,
       _74283_2_pin13, _74283_2_pin15, xor_1_out, xor_2_out, xor_5_out, xor_6_out;

  xor xor_1 (xor_1_out, SUB, B_1);
  xor xor_2 (xor_2_out, SUB, B_0);
  LED S_7 (.in(_74283_2_pin10));
  _74283 _74283_1 (
    .pin1(_74283_1_pin1), .pin2(xor_1_out), .pin3(A_1), .pin4(_74283_1_pin4), .pin5(A_0), .pin6(xor_2_out),
    .pin7(SUB), .pin8(1'b0), .pin9(_74283_1_pin9), .pin10(_74283_1_pin10), .pin11(_74283_1_pin11),
    .pin12(A_3), .pin13(_74283_1_pin13), .pin14(A_2), .pin15(_74283_1_pin15), .pin16(1'b1));
  LED S_6 (.in(_74283_2_pin13));
  LED S_5 (.in(_74283_2_pin1));
  xor xor_3 (_74283_1_pin15, SUB, B_2);
  xor xor_4 (_74283_1_pin11, SUB, B_3);
  LED S_4 (.in(_74283_2_pin4));
  xor xor_5 (xor_5_out, B_5, SUB);
  xor xor_6 (xor_6_out, B_4, SUB);
  LED S_3 (.in(_74283_1_pin10));
  LED S_2 (.in(_74283_1_pin13));
  _74283 _74283_2 (
    .pin1(_74283_2_pin1), .pin2(xor_5_out), .pin3(A_5), .pin4(_74283_2_pin4), .pin5(A_4), .pin6(xor_6_out),
    .pin7(_74283_1_pin9), .pin8(1'b0), .pin9(_74283_2_pin9), .pin10(_74283_2_pin10), .pin11(_74283_2_pin11),
    .pin12(A_7), .pin13(_74283_2_pin13), .pin14(A_6), .pin15(_74283_2_pin15), .pin16(1'b1));
  LED S_1 (.in(_74283_1_pin1));
  LED S_0 (.in(_74283_1_pin4));
  xor xor_7 (_74283_2_pin15, SUB, B_6);
  xor xor_8 (_74283_2_pin11, SUB, B_7);
  LED C_out (.in(_74283_2_pin9));
endmodule
